# Fritzing sketch CRA (saved by Fritzing 0.9.3b)
breadboards: 1

parts:
  Accelerometer = Triple Axis Accelerometer Breakout - ADXL345
  Raspberry_Pi_4_Model_B = Raspberry Pi 3 [part_number=RPI-3-V1.2]

nets:
  GND: Accelerometer.GND, Raspberry_Pi_4_Model_B.GND
  VCC: Accelerometer.VCC, Raspberry_Pi_4_Model_B.3v3
  N1: Accelerometer.SDA, Raspberry_Pi_4_Model_B.GPIO2
  N2: Accelerometer.SCL, Raspberry_Pi_4_Model_B.GPIO3
